# Fritzing sketch connect relay (saved by Fritzing 1.0.0rc)

parts:
  Power_plug1 = Power plug
  U2 = V18ZA2P [package=v18za2p]
  KY-1 = Keyes Relay [package=THT]
  ESP1 = ESP 12E
  AMS1117_on_PCB = Voltage Regulator - Variable [package="TO220 [THT]"]

nets:
  N1: Power_plug1.GND, U2.-
  N2: Power_plug1.VCC, KY-1.NO
  N3: U2.+, KY-1.C
  N4: KY-1.signal, ESP1.GPIO12
  N5: KY-1.power, AMS1117_on_PCB.IN
  N6: KY-1.ground, AMS1117_on_PCB.ADJ

custom parts:
  V18ZA2P: Varistor
  Keyes Relay: The Keyes 5V relay module is suitable for SCM development, home appliance control. It uses a 5V~12V TIL control signal which can control DC / AC signal.
  ESP 12E: ESP 12e module with spi interface and wifi connection
