# Fritzing sketch connect uln2003 (saved by Fritzing 1.0.0rc)

parts:
  Power_plug1 = Power plug
  ESP1 = ESP 12E
  IC1 = ULN2003A [package="SO16 [SMD]"]
  AMS1117_on_PCB = Voltage Regulator [package=to220-adj]
  RY1 = srd-05vdc-sl-c
  U2 = V18ZA2P [package=v18za2p]

nets:
  N1: Power_plug1.GND, U2.-
  N2: Power_plug1.VCC, RY1.pin_4
  N3: ESP1.GPIO12, IC1.In_4
  N4: IC1.0V, AMS1117_on_PCB.ADJ
  N5: IC1.COM_-_Common, AMS1117_on_PCB.OUT, RY1.pin_2
  N6: IC1.Out_4, RY1.pin_3
  N7: RY1.pin_5, U2.+

custom parts:
  ESP 12E: ESP 12e module with spi interface and wifi connection
  V18ZA2P: Varistor
