# Fritzing sketch connect-relay (saved by Fritzing 1.0.0rc)

parts:
  KY-1 = Keyes Relay [package=THT]
  ESP1 = ESP 12E
  AMS1117_on_PCB = Voltage Regulator - Variable [package="TO220 [THT]"]
  J1 = 220v plug

nets:
  N1: KY-1.signal, ESP1.GPIO12
  N2: KY-1.power, AMS1117_on_PCB.IN
  N3: KY-1.ground, AMS1117_on_PCB.ADJ
  N4: KY-1.NO, J1.pin1

notes:
  220v Output

custom parts:
  Keyes Relay: The Keyes 5V relay module is suitable for SCM development, home appliance control. It uses a 5V~12V TIL control signal which can control DC / AC signal.
  ESP 12E: ESP 12e module with spi interface and wifi connection
  220v plug: Generic 220V AC plug.
