# Fritzing sketch connect-uln2003-led (saved by Fritzing 1.0.0rc)

parts:
  ESP1 = ESP 12E
  IC1 = ULN2003A [package="SO16 [SMD]"]
  AMS1117_on_PCB = Voltage Regulator [package=to220-adj]
  LED1 = LED - 5mm [color="Red (633nm)" current=0.030A package="5 mm [THT]"]

nets:
  N1: ESP1.GPIO12, IC1.In_4
  N2: IC1.0V, AMS1117_on_PCB.ADJ
  N3: IC1.COM_-_Common, AMS1117_on_PCB.OUT, LED1.anode
  N4: IC1.Out_4, LED1.cathode

custom parts:
  ESP 12E: ESP 12e module with spi interface and wifi connection
