# Fritzing sketch connect-uln2003 (saved by Fritzing 1.0.0rc)

parts:
  ESP1 = ESP 12E
  IC1 = ULN2003A [package="SO16 [SMD]"]
  AMS1117_on_PCB = Voltage Regulator [package=to220-adj]
  RY1 = srd-05vdc-sl-c
  J1 = 220v plug

nets:
  N1: ESP1.GPIO12, IC1.In_4
  N2: IC1.0V, AMS1117_on_PCB.ADJ
  N3: IC1.COM_-_Common, AMS1117_on_PCB.OUT, RY1.pin_2
  N4: IC1.Out_4, RY1.pin_3
  N5: RY1.pin_4, J1.pin1

notes:
  220v Output

custom parts:
  ESP 12E: ESP 12e module with spi interface and wifi connection
  220v plug: Generic 220V AC plug.
